// Logisim project project.circ as structural Verilog: 1 circuit, main circuit main
module main (
);

  wire and_1_out, and_2_out, and_3_out, and_4_out, and_5_out, and_6_out, and_7_out, and_8_out, and_9_out,
       clock_1_out, not_1_out, not_2_out, not_3_out, not_4_out, not_5_out, or_1_out, or_2_out, t_ff_1_q,
       t_ff_1_qn, t_ff_2_q, t_ff_2_qn;
  wire [5:0] counter_1_q;

  Clock clock_1 (.out(clock_1_out));
  Counter #(.width(6), .max('h3f)) counter_1 (
    .Q(counter_1_q), .clk(clock_1_out), .clr(and_1_out));  // open: load, D, count, carry
  and and_1 (and_1_out, counter_1_q[0], counter_1_q[2], counter_1_q[3], counter_1_q[4], counter_1_q[5]);
  not not_1 (not_1_out, counter_1_q[2]);
  not not_2 (not_2_out, counter_1_q[5]);
  not not_3 (not_3_out, counter_1_q[0]);
  not not_4 (not_4_out, counter_1_q[1]);
  not not_5 (not_5_out, counter_1_q[2]);
  and and_2 (and_2_out, counter_1_q[0], counter_1_q[1], not_1_out, counter_1_q[3], counter_1_q[4], not_2_out);
  and and_3 (and_3_out, not_3_out, counter_1_q[1], counter_1_q[2], counter_1_q[3], counter_1_q[4]);
  and and_4 (and_4_out, counter_1_q[2], counter_1_q[3], counter_1_q[4], counter_1_q[5]);
  and and_5 (and_5_out, counter_1_q[0], not_4_out, not_5_out, counter_1_q[3], counter_1_q[4], counter_1_q[5]);
  or or_1 (or_1_out, and_3_out, and_4_out);
  or or_2 (or_2_out, and_2_out, and_3_out, and_4_out, and_5_out);
  T_Flip_Flop t_ff_1 (.clk(clock_1_out), .T(or_1_out), .Q(t_ff_1_q), .Qn(t_ff_1_qn));  // open: preset, reset, en
  T_Flip_Flop t_ff_2 (.clk(clock_1_out), .T(or_2_out), .Q(t_ff_2_q), .Qn(t_ff_2_qn));  // open: preset, reset, en
  and and_6 (and_6_out, t_ff_1_qn, t_ff_2_qn);
  and and_7 (and_7_out, t_ff_1_qn, t_ff_2_q);
  LED red (.in(t_ff_1_qn));
  LED green (.in(and_6_out));
  LED yellow (.in(and_7_out));
  LED red_2 (.in(t_ff_1_q));
  LED green_2 (.in(and_9_out));
  and and_8 (and_8_out, t_ff_1_q, t_ff_2_q);
  LED yellow_2 (.in(and_8_out));
  LED yellow_3 (.in(and_8_out));
  and and_9 (and_9_out, t_ff_1_q, t_ff_2_qn);
  LED green_3 (.in(and_9_out));
  LED red_3 (.in(t_ff_1_q));
  LED yellow_4 (.in(and_7_out));
  LED green_4 (.in(and_6_out));
  LED red_4 (.in(t_ff_1_qn));
endmodule
